# Fritzing sketch stairs-light (saved by Fritzing 0.9.3b)
breadboards: 1

parts:
  R1 = Trimmer Potentiometer [maximum_resistance=10kΩ package=THT]
  Part1 = Arduino Nano (Rev3.0)
  hc-sr1 = hc-sr04
  hc-sr2 = hc-sr04
  KY-1 = Keyes Relay [package=THT]
  R4 = Resistor [tolerance=±5% resistance=10k package="0805 [SMD]"]
  R5 = Photocell (LDR) [package=THT]

nets:
  GND: R1.leg1, Part1.GND, hc-sr1.GND, hc-sr2.GND, KY-1.ground, R5.pin_1
  N1: R1.wiper, Part1.A3
  VCC: R1.leg2, Part1.5V, hc-sr1.VCC, hc-sr2.VCC, KY-1.signal, R4.Pin_1
  N2: Part1.D2, KY-1.power
  N3: Part1.D5, hc-sr2.Echo
  N4: Part1.D6, hc-sr2.Trig
  N5: Part1.D7, hc-sr1.Echo
  N6: Part1.D8, hc-sr1.Trig
  N7: Part1.A1, R4.Pin_0, R5.pin_0

custom parts:
  Keyes Relay: The Keyes 5V relay module is suitable for SCM development, home appliance control. It uses a 5V~12V TIL control signal which can control DC / AC signal.
